# Fritzing sketch blnuhr_led (saved by Fritzing 0.9.3b)

parts:
  R5 = Resistor [tolerance=±5% resistance=220 package=THT]
  R6 = Resistor [tolerance=±5% resistance=220 package=THT]
  R7 = Resistor [tolerance=±5% resistance=220 package=THT]
  R8 = Resistor [tolerance=±5% resistance=220 package=THT]
  R9 = Resistor [tolerance=±5% resistance=220 package=THT]
  R10 = Resistor [tolerance=±5% resistance=220 package=THT]
  R11 = Resistor [tolerance=±5% resistance=220 package=THT]
  R12 = Resistor [tolerance=±5% resistance=220 package=THT]
  R13 = Resistor [tolerance=±5% resistance=220 package=THT]
  R14 = Resistor [tolerance=±5% resistance=220 package=THT]
  R16 = Resistor [tolerance=±5% resistance=220 package=THT]
  R17 = Resistor [tolerance=±5% resistance=220 package=THT]
  R18 = Resistor [tolerance=±5% resistance=220 package=THT]
  R19 = Resistor [tolerance=±5% resistance=220 package=THT]
  R20 = Resistor [tolerance=±5% resistance=220 package=THT]
  R21 = Resistor [tolerance=±5% resistance=220 package=THT]
  R22 = Resistor [tolerance=±5% resistance=220 package=THT]
  R23 = Resistor [tolerance=±5% resistance=220 package=THT]
  R24 = Resistor [tolerance=±5% resistance=220 package=THT]
  R25 = Resistor [tolerance=±5% resistance=220 package=THT]
  R26 = Resistor [tolerance=±5% resistance=220 package=THT]
  R27 = Resistor [tolerance=±5% resistance=220 package=THT]
  R28 = Resistor [tolerance=±5% resistance=220 package=THT]
  R29 = Resistor [tolerance=±5% resistance=220 package=THT]
  Part1 = Arduino Mega Proto Shield
  J5 = female pin header, 4 pins [form="♀ (female)"]
  J14 = female pin header, 11 pins [form="♀ (female)"]
  J15 = female pin header, 11 pins [form="♀ (female)"]
  J16 = female pin header, 2 pins [form="♀ (female)"]
  J17 = female pin header, 4 pins [form="♀ (female)"]
  J18 = female pin header, 4 pins [form="♀ (female)"]
  J20 = female pin header, 4 pins [form="♀ (female)"]
  J21 = female pin header, 4 pins [form="♀ (female)"]
  J19 = female pin header, 4 pins [form="♀ (female)"]

nets:
  N1: R5.Pin_0, R6.Pin_0, R7.Pin_0, R8.Pin_0, R9.Pin_0, R10.Pin_0, R11.Pin_0, R12.Pin_0, R13.Pin_0, R14.Pin_0, R16.Pin_0, R17.Pin_0, R18.Pin_0, R19.Pin_0, R20.Pin_0, R21.Pin_0, R22.Pin_0, R23.Pin_0, R24.Pin_0, R25.Pin_0, R26.Pin_0, R27.Pin_0, R28.Pin_0, R29.Pin_0, Part1.5V@1
  N2: R5.Pin_1, Part1.N$130, Part1.N$131, J14.pin10
  N3: R6.Pin_1, Part1.N$142, Part1.N$143, J14.pin9
  N4: R7.Pin_1, Part1.N$113, Part1.N$114, J14.pin11
  N5: R8.Pin_1, Part1.N$170, Part1.N$171, J14.pin7
  N6: R9.Pin_1, Part1.N$184, Part1.N$185, J14.pin6
  N7: R10.Pin_1, Part1.N$156, Part1.N$157, J14.pin8
  N8: R11.Pin_1, Part1.N$212, Part1.N$213, J14.pin4
  N9: R12.Pin_1, Part1.N$226, Part1.N$227, J14.pin3
  N10: R13.Pin_1, Part1.N$198, Part1.N$199, J14.pin5
  N11: R14.Pin_1, Part1.N$254, Part1.N$255, J14.pin1
  N12: R16.Pin_1, Part1.N$240, Part1.N$241, J14.pin2
  N13: R17.Pin_1, Part1.N$296, Part1.N$297, J20.pin3
  N14: R18.Pin_1, Part1.N$332, Part1.N$333, J20.pin1
  N15: R19.Pin_1, Part1.N$310, Part1.N$311, J20.pin2
  N16: R20.Pin_1, Part1.N$282, Part1.N$284, J20.pin4
  N17: R21.Pin_1, Part1.N$381, Part1.N$382, J5.pin3
  N18: R22.Pin_1, Part1.N$441, Part1.N$442, J5.pin1
  N19: R23.Pin_1, Part1.N$425, Part1.N$426, J5.pin2
  N20: R24.Pin_1, Part1.N$365, Part1.N$367, J5.pin4
  N21: R25.Pin_1, Part1.N$444, Part1.N$500, J16.pin1
  N22: R26.Pin_1, Part1.N$55, Part1.N$56, J18.pin4
  N23: R27.Pin_1, Part1.N$65, Part1.N$66, J18.pin3
  N24: R28.Pin_1, Part1.N$79, Part1.N$80, J18.pin2
  N25: R29.Pin_1, Part1.N$89, Part1.N$90, J18.pin1
  N26: Part1.N$54, J19.pin4
  N27: Part1.N$67, J19.pin3
  N28: Part1.N$78, J19.pin2
  N29: Part1.N$91, J19.pin1
  N30: Part1.N$115, J15.pin11
  N31: Part1.N$129, J15.pin10
  N32: Part1.N$144, J15.pin9
  N33: Part1.N$155, J15.pin8
  N34: Part1.N$172, J15.pin7
  N35: Part1.N$183, J15.pin6
  N36: Part1.N$200, J15.pin5
  N37: Part1.N$211, J15.pin4
  N38: Part1.N$228, J15.pin3
  N39: Part1.N$239, J15.pin2
  N40: Part1.N$256, J15.pin1
  N41: Part1.N$283, J21.pin4
  N42: Part1.N$295, J21.pin3
  N43: Part1.N$325, J21.pin2
  N44: Part1.N$334, J21.pin1
  N45: Part1.N$366, J17.pin4
  N46: Part1.N$380, J17.pin3
  N47: Part1.N$427, J17.pin2
  N48: Part1.N$440, J17.pin1
  N49: Part1.N$447, J16.pin2
