# Fritzing sketch blnuhr (saved by Fritzing 0.9.2b)
circuit board: 18.3823cm x 7.94313cm
breadboards: 1

parts:
  R1 = Resistor [tolerance=±5% resistance=1k package=THT]
  LED1 = LED - 5mm [color="Orange (612nm)" package="5 mm [THT]"]
  R2 = Resistor [tolerance=±5% resistance=1k package=THT]
  LED2 = LED - 5mm [color="Red (635nm)" package="5 mm [THT]"]
  R3 = Resistor [tolerance=±5% resistance=1k package=THT]
  LED3 = LED - 5mm [color="Red (635nm)" package="5 mm [THT]"]
  R4 = Resistor [tolerance=±5% resistance=1k package=THT]
  R5 = Resistor [tolerance=±5% resistance=1k package=THT]
  LED4 = LED - 5mm [color="Red (635nm)" package="5 mm [THT]"]
  LED5 = LED - 5mm [color="Red (635nm)" package="5 mm [THT]"]
  R6 = Resistor [tolerance=±5% resistance=1k package=THT]
  R7 = Resistor [tolerance=±5% resistance=1k package=THT]
  R8 = Resistor [tolerance=±5% resistance=1k package=THT]
  R9 = Resistor [tolerance=±5% resistance=1k package=THT]
  LED6 = LED - 5mm [color="Red (635nm)" package="5 mm [THT]"]
  LED7 = LED - 5mm [color="Red (635nm)" package="5 mm [THT]"]
  LED8 = LED - 5mm [color="Red (635nm)" package="5 mm [THT]"]
  LED9 = LED - 5mm [color="Red (635nm)" package="5 mm [THT]"]
  R10 = Resistor [tolerance=±5% resistance=1k package=THT]
  R11 = Resistor [tolerance=±5% resistance=1k package=THT]
  R12 = Resistor [tolerance=±5% resistance=1k package=THT]
  LED10 = LED - 5mm [color="Orange (612nm)" package="5 mm [THT]"]
  LED11 = LED - 5mm [color="Orange (612nm)" package="5 mm [THT]"]
  LED12 = LED - 5mm [color="Red (635nm)" package="5 mm [THT]"]
  R13 = Resistor [tolerance=±5% resistance=1k package=THT]
  R14 = Resistor [tolerance=±5% resistance=1k package=THT]
  R15 = Resistor [tolerance=±5% resistance=1k package=THT]
  LED13 = LED - 5mm [color="Orange (612nm)" package="5 mm [THT]"]
  LED14 = LED - 5mm [color="Orange (612nm)" package="5 mm [THT]"]
  LED15 = LED - 5mm [color="Red (635nm)" package="5 mm [THT]"]
  R16 = Resistor [tolerance=±5% resistance=1k package=THT]
  R17 = Resistor [tolerance=±5% resistance=1k package=THT]
  R18 = Resistor [tolerance=±5% resistance=1k package=THT]
  LED16 = LED - 5mm [color="Orange (612nm)" package="5 mm [THT]"]
  LED17 = LED - 5mm [color="Orange (612nm)" package="5 mm [THT]"]
  LED18 = LED - 5mm [color="Red (635nm)" package="5 mm [THT]"]
  R19 = Resistor [tolerance=±5% resistance=1k package=THT]
  R20 = Resistor [tolerance=±5% resistance=1k package=THT]
  LED19 = LED - 5mm [color="Orange (612nm)" package="5 mm [THT]"]
  LED20 = LED - 5mm [color="Orange (612nm)" package="5 mm [THT]"]
  R21 = Resistor [tolerance=±5% resistance=1k package=THT]
  R22 = Resistor [tolerance=±5% resistance=1k package=THT]
  LED21 = LED - 5mm [color="Orange (612nm)" package="5 mm [THT]"]
  LED22 = LED - 5mm [color="Orange (612nm)" package="5 mm [THT]"]
  R23 = Resistor [tolerance=±5% resistance=1k package=THT]
  R24 = Resistor [tolerance=±5% resistance=1k package=THT]
  LED23 = LED - 5mm [color="Orange (612nm)" package="5 mm [THT]"]
  LED24 = LED - 5mm [color="Orange (612nm)" package="5 mm [THT]"]
  J1 = male pin header, 25 pins [form="♂ (male)"]
  Pad2 = Pad [width=4.25782253265694 height=4.33496987036101 connect=center]
  Pad3 = Pad [width=4.25782253265694 height=4.33496987036101 connect=center]
  Pad4 = Pad [width=4.25782253265694 height=4.33496987036101 connect=center]
  Pad5 = Pad [width=4.25782253265694 height=4.33496987036101 connect=center]
  Pad6 = Pad [width=4.25782253265694 height=4.33496987036101 connect=center]
  Pad7 = Pad [width=4.25782253265694 height=4.33496987036101 connect=center]

nets:
  N1: R1.Pin_0, LED1.anode
  N2: R1.Pin_1, J1.pin1
  N3: LED1.cathode, LED2.cathode, LED3.cathode, LED4.cathode, LED5.cathode, LED6.cathode, LED7.cathode, LED8.cathode, LED9.cathode, LED10.cathode, LED11.cathode, LED12.cathode, LED13.cathode, LED14.cathode, LED15.cathode, LED16.cathode, LED17.cathode, LED18.cathode, LED19.cathode, LED20.cathode, LED21.cathode, LED22.cathode, LED23.cathode, LED24.cathode, J1.pin25, Pad2.pad, Pad3.pad, Pad4.pad, Pad5.pad, Pad6.pad, Pad7.pad
  N4: R2.Pin_0, LED2.anode
  N5: R2.Pin_1, J1.pin2
  N6: R3.Pin_0, LED3.anode
  N7: R3.Pin_1, J1.pin3
  N8: R4.Pin_0, LED4.anode
  N9: R4.Pin_1, J1.pin4
  N10: R5.Pin_0, LED5.anode
  N11: R5.Pin_1, J1.pin5
  N12: R6.Pin_0, LED6.anode
  N13: R6.Pin_1, J1.pin6
  N14: R7.Pin_0, LED7.anode
  N15: R7.Pin_1, J1.pin7
  N16: R8.Pin_0, LED8.anode
  N17: R8.Pin_1, J1.pin8
  N18: R9.Pin_0, LED9.anode
  N19: R9.Pin_1, J1.pin9
  N20: R10.Pin_0, LED10.anode
  N21: R10.Pin_1, J1.pin10
  N22: R11.Pin_0, LED11.anode
  N23: R11.Pin_1, J1.pin11
  N24: R12.Pin_0, LED12.anode
  N25: R12.Pin_1, J1.pin12
  N26: R13.Pin_0, LED13.anode
  N27: R13.Pin_1, J1.pin13
  N28: R14.Pin_0, LED14.anode
  N29: R14.Pin_1, J1.pin14
  N30: R15.Pin_0, LED15.anode
  N31: R15.Pin_1, J1.pin15
  N32: R16.Pin_0, LED16.anode
  N33: R16.Pin_1, J1.pin16
  N34: R17.Pin_0, LED17.anode
  N35: R17.Pin_1, J1.pin17
  N36: R18.Pin_0, LED18.anode
  N37: R18.Pin_1, J1.pin18
  N38: R19.Pin_0, LED19.anode
  N39: R19.Pin_1, J1.pin19
  N40: R20.Pin_0, LED20.anode
  N41: R20.Pin_1, J1.pin20
  N42: R21.Pin_0, LED21.anode
  N43: R21.Pin_1, J1.pin21
  N44: R22.Pin_0, LED22.anode
  N45: R22.Pin_1, J1.pin22
  N46: R23.Pin_0, LED23.anode
  N47: R23.Pin_1, J1.pin23
  N48: R24.Pin_0, LED24.anode
  N49: R24.Pin_1, J1.pin24
