# Fritzing sketch 2-connector (saved by Fritzing 0.9.2b)
circuit board: 19.1102cm x 16.5798cm
breadboards: 1

parts:
  LED1 = LED - 5mm [color="Red (633nm)" package="5 mm [THT]"]
  LED2 = LED - 5mm [color="Red (633nm)" package="5 mm [THT]"]
  LED3 = LED - 5mm [color="Red (633nm)" package="5 mm [THT]"]
  LED4 = LED - 5mm [color="Red (633nm)" package="5 mm [THT]"]
  LED5 = LED - 5mm [color="Red (633nm)" package="5 mm [THT]"]
  R1 = Resistor [tolerance=±5% resistance=220 package=THT]
  R2 = Resistor [tolerance=±5% resistance=220 package=THT]
  R3 = Resistor [tolerance=±5% resistance=220 package=THT]
  R4 = Resistor [tolerance=±5% resistance=220 package=THT]
  R5 = Resistor [tolerance=±5% resistance=220 package=THT]
  LED8 = LED - 5mm [color="Red (633nm)" package="5 mm [THT]"]
  LED9 = LED - 5mm [color="Red (633nm)" package="5 mm [THT]"]
  LED7 = LED - 5mm [color="Red (633nm)" package="5 mm [THT]"]
  LED6 = LED - 5mm [color="Red (633nm)" package="5 mm [THT]"]
  R7 = Resistor [tolerance=±5% resistance=220 package=THT]
  R9 = Resistor [tolerance=±5% resistance=220 package=THT]
  R6 = Resistor [tolerance=±5% resistance=220 package=THT]
  R8 = Resistor [tolerance=±5% resistance=220 package=THT]
  LED13 = LED - 5mm [color="Red (633nm)" package="5 mm [THT]"]
  LED11 = LED - 5mm [color="Red (633nm)" package="5 mm [THT]"]
  LED10 = LED - 5mm [color="Red (633nm)" package="5 mm [THT]"]
  LED12 = LED - 5mm [color="Red (633nm)" package="5 mm [THT]"]
  R10 = Resistor [tolerance=±5% resistance=220 package=THT]
  R12 = Resistor [tolerance=±5% resistance=220 package=THT]
  R13 = Resistor [tolerance=±5% resistance=220 package=THT]
  R11 = Resistor [tolerance=±5% resistance=220 package=THT]
  LED14 = LED - 5mm [color="Red (633nm)" package="5 mm [THT]"]
  R14 = Resistor [tolerance=±5% resistance=220 package=THT]
  LED15 = LED - 5mm [color="Red (633nm)" package="5 mm [THT]"]
  R15 = Resistor [tolerance=±5% resistance=220 package=THT]
  LED16 = LED - 5mm [color="Red (633nm)" package="5 mm [THT]"]
  R16 = Resistor [tolerance=±5% resistance=220 package=THT]
  LED17 = LED - 5mm [color="Red (633nm)" package="5 mm [THT]"]
  R17 = Resistor [tolerance=±5% resistance=220 package=THT]
  LED18 = LED - 5mm [color="Red (633nm)" package="5 mm [THT]"]
  R18 = Resistor [tolerance=±5% resistance=220 package=THT]
  LED19 = LED - 5mm [color="Red (633nm)" package="5 mm [THT]"]
  R19 = Resistor [tolerance=±5% resistance=220 package=THT]
  LED20 = LED - 5mm [color="Red (633nm)" package="5 mm [THT]"]
  R20 = Resistor [tolerance=±5% resistance=220 package=THT]
  LED24 = LED - 5mm [color="Orange (612nm)" package="5 mm [THT]"]
  LED23 = LED - 5mm [color="Red (633nm)" package="5 mm [THT]"]
  LED21 = LED - 5mm [color="Red (633nm)" package="5 mm [THT]"]
  LED22 = LED - 5mm [color="Red (633nm)" package="5 mm [THT]"]
  R21 = Resistor [tolerance=±5% resistance=220 package=THT]
  R22 = Resistor [tolerance=±5% resistance=220 package=THT]
  R24 = Resistor [tolerance=±5% resistance=220 package=THT]
  R23 = Resistor [tolerance=±5% resistance=220 package=THT]
  J1 = female pin header, 18 pins [form="♀ (female)"]
  J2 = female pin header, 18 pins [form="♀ (female)"]
  R25 = Resistor [tolerance=±5% resistance=10k package=THT]
  R26 = Resistor [tolerance=±5% resistance=10k package=THT]
  S1 = Pushbutton [package=THT]
  S2 = Pushbutton [package=THT]

nets:
  N1: LED1.cathode, LED2.cathode, LED3.cathode, LED4.cathode, LED5.cathode, LED8.cathode, LED9.cathode, LED7.cathode, LED6.cathode, J1.pin18
  N2: LED1.anode, R1.Pin_0
  N3: LED2.anode, R2.Pin_0
  N4: LED3.anode, R3.Pin_0
  N5: LED4.anode, R4.Pin_0
  N6: LED5.anode, R5.Pin_0
  N7: R1.Pin_1, J1.pin9
  N8: R2.Pin_1, J1.pin13
  N9: R3.Pin_1, J1.pin12
  N10: R4.Pin_1, J1.pin11
  N11: R5.Pin_1, J1.pin10
  N12: LED8.anode, R8.Pin_0
  N13: LED9.anode, R9.Pin_0
  N14: LED7.anode, R7.Pin_0
  N15: LED6.anode, R6.Pin_0
  N16: R7.Pin_1, J1.pin16
  N17: R9.Pin_1, J1.pin14
  N18: R6.Pin_1, J1.pin17
  N19: R8.Pin_1, J1.pin15
  N20: LED13.cathode, LED11.cathode, LED10.cathode, LED12.cathode, LED14.cathode, LED15.cathode, LED16.cathode, LED17.cathode, LED18.cathode, LED19.cathode, LED20.cathode, LED24.cathode, LED23.cathode, LED21.cathode, LED22.cathode, J2.pin18
  N21: LED13.anode, R13.Pin_0
  N22: LED11.anode, R11.Pin_0
  N23: LED10.anode, R10.Pin_0
  N24: LED12.anode, R12.Pin_0
  N25: R10.Pin_1, J2.pin13
  N26: R12.Pin_1, J2.pin11
  N27: R13.Pin_1, J2.pin10
  N28: R11.Pin_1, J2.pin12
  N29: LED14.anode, R14.Pin_0
  N30: R14.Pin_1, J2.pin9
  N31: LED15.anode, R15.Pin_0
  N32: R15.Pin_1, J2.pin8
  N33: LED16.anode, R16.Pin_0
  N34: R16.Pin_1, J2.pin7
  N35: LED17.anode, R17.Pin_0
  N36: R17.Pin_1, J2.pin6
  N37: LED18.anode, R18.Pin_0
  N38: R18.Pin_1, J2.pin5
  N39: LED19.anode, R19.Pin_0
  N40: R19.Pin_1, J2.pin4
  N41: LED20.anode, R20.Pin_0
  N42: R20.Pin_1, J2.pin3
  N43: LED24.anode, R24.Pin_0
  N44: LED23.anode, R23.Pin_0
  N45: LED21.anode, R21.Pin_0
  N46: LED22.anode, R22.Pin_0
  N47: R21.Pin_1, J2.pin17
  N48: R22.Pin_1, J2.pin16
  N49: R24.Pin_1, J2.pin14
  N50: R23.Pin_1, J2.pin15
  N51: J1.pin1, S1.leg1, S2.leg1
  N52: J1.pin7, R25.Pin_0
  N53: J1.pin8, R26.Pin_0
  N54: R25.Pin_1, S2.leg0
  N55: R26.Pin_1, S1.leg0

notes:
  blnuhr rev. A
  (C) 2016 Pete R. Jemian
  serial #
  blnuhr.readthedocs.org
