# Fritzing sketch 4-connectors (saved by Fritzing 0.9.2b)
circuit board: 18.3659cm x 13.135cm
breadboards: 1

parts:
  LED1 = LED - 5mm [color="Red (633nm)" package="5 mm [THT]"]
  LED2 = LED - 5mm [color="Red (633nm)" package="5 mm [THT]"]
  LED3 = LED - 5mm [color="Red (633nm)" package="5 mm [THT]"]
  LED4 = LED - 5mm [color="Red (633nm)" package="5 mm [THT]"]
  LED5 = LED - 5mm [color="Red (633nm)" package="5 mm [THT]"]
  R1 = Resistor [tolerance=±5% resistance=220 package=THT]
  J1 = male pin header, 6 pins [form="♂ (male)"]
  R2 = Resistor [tolerance=±5% resistance=220 package=THT]
  R3 = Resistor [tolerance=±5% resistance=220 package=THT]
  R4 = Resistor [tolerance=±5% resistance=220 package=THT]
  R5 = Resistor [tolerance=±5% resistance=220 package=THT]
  LED8 = LED - 5mm [color="Red (633nm)" package="5 mm [THT]"]
  LED9 = LED - 5mm [color="Red (633nm)" package="5 mm [THT]"]
  LED7 = LED - 5mm [color="Red (633nm)" package="5 mm [THT]"]
  LED6 = LED - 5mm [color="Red (633nm)" package="5 mm [THT]"]
  R7 = Resistor [tolerance=±5% resistance=220 package=THT]
  R9 = Resistor [tolerance=±5% resistance=220 package=THT]
  R6 = Resistor [tolerance=±5% resistance=220 package=THT]
  R8 = Resistor [tolerance=±5% resistance=220 package=THT]
  LED13 = LED - 5mm [color="Red (633nm)" package="5 mm [THT]"]
  LED11 = LED - 5mm [color="Red (633nm)" package="5 mm [THT]"]
  LED10 = LED - 5mm [color="Red (633nm)" package="5 mm [THT]"]
  LED12 = LED - 5mm [color="Red (633nm)" package="5 mm [THT]"]
  R10 = Resistor [tolerance=±5% resistance=220 package=THT]
  R12 = Resistor [tolerance=±5% resistance=220 package=THT]
  R13 = Resistor [tolerance=±5% resistance=220 package=THT]
  R11 = Resistor [tolerance=±5% resistance=220 package=THT]
  J2 = male pin header, 4 pins [form="♂ (male)"]
  J3 = male pin header, 11 pins [form="♂ (male)"]
  LED14 = LED - 5mm [color="Red (633nm)" package="5 mm [THT]"]
  R14 = Resistor [tolerance=±5% resistance=220 package=THT]
  LED15 = LED - 5mm [color="Red (633nm)" package="5 mm [THT]"]
  R15 = Resistor [tolerance=±5% resistance=220 package=THT]
  LED16 = LED - 5mm [color="Red (633nm)" package="5 mm [THT]"]
  R16 = Resistor [tolerance=±5% resistance=220 package=THT]
  LED17 = LED - 5mm [color="Red (633nm)" package="5 mm [THT]"]
  R17 = Resistor [tolerance=±5% resistance=220 package=THT]
  LED18 = LED - 5mm [color="Red (633nm)" package="5 mm [THT]"]
  R18 = Resistor [tolerance=±5% resistance=220 package=THT]
  LED19 = LED - 5mm [color="Red (633nm)" package="5 mm [THT]"]
  R19 = Resistor [tolerance=±5% resistance=220 package=THT]
  LED20 = LED - 5mm [color="Red (633nm)" package="5 mm [THT]"]
  R20 = Resistor [tolerance=±5% resistance=220 package=THT]
  LED24 = LED - 5mm [color="Orange (612nm)" package="5 mm [THT]"]
  LED23 = LED - 5mm [color="Red (633nm)" package="5 mm [THT]"]
  LED21 = LED - 5mm [color="Red (633nm)" package="5 mm [THT]"]
  LED22 = LED - 5mm [color="Red (633nm)" package="5 mm [THT]"]
  J4 = male pin header, 4 pins [form="♂ (male)"]
  R21 = Resistor [tolerance=±5% resistance=220 package=THT]
  R22 = Resistor [tolerance=±5% resistance=220 package=THT]
  R24 = Resistor [tolerance=±5% resistance=220 package=THT]
  R23 = Resistor [tolerance=±5% resistance=220 package=THT]

nets:
  N1: LED1.cathode, LED2.cathode, LED3.cathode, LED4.cathode, LED5.cathode, J1.pin6, LED8.cathode, LED9.cathode, LED7.cathode, LED6.cathode, LED13.cathode, LED11.cathode, LED10.cathode, LED12.cathode, LED14.cathode, LED15.cathode, LED16.cathode, LED17.cathode, LED18.cathode, LED19.cathode, LED20.cathode, LED24.cathode, LED23.cathode, LED21.cathode, LED22.cathode
  N2: LED1.anode, R1.Pin_0
  N3: LED2.anode, R2.Pin_0
  N4: LED3.anode, R3.Pin_0
  N5: LED4.anode, R4.Pin_0
  N6: LED5.anode, R5.Pin_0
  N7: R1.Pin_1, J1.pin1
  N8: J1.pin2, R5.Pin_1
  N9: J1.pin3, R4.Pin_1
  N10: J1.pin4, R3.Pin_1
  N11: J1.pin5, R2.Pin_1
  N12: LED8.anode, R8.Pin_0
  N13: LED9.anode, R9.Pin_0
  N14: LED7.anode, R7.Pin_0
  N15: LED6.anode, R6.Pin_0
  N16: R7.Pin_1, J2.pin3
  N17: R9.Pin_1, J2.pin1
  N18: R6.Pin_1, J2.pin4
  N19: R8.Pin_1, J2.pin2
  N20: LED13.anode, R13.Pin_0
  N21: LED11.anode, R11.Pin_0
  N22: LED10.anode, R10.Pin_0
  N23: LED12.anode, R12.Pin_0
  N24: R10.Pin_1, J3.pin11
  N25: R12.Pin_1, J3.pin9
  N26: R13.Pin_1, J3.pin8
  N27: R11.Pin_1, J3.pin10
  N28: J3.pin1, R20.Pin_1
  N29: J3.pin2, R19.Pin_1
  N30: J3.pin3, R18.Pin_1
  N31: J3.pin4, R17.Pin_1
  N32: J3.pin5, R16.Pin_1
  N33: J3.pin6, R15.Pin_1
  N34: J3.pin7, R14.Pin_1
  N35: LED14.anode, R14.Pin_0
  N36: LED15.anode, R15.Pin_0
  N37: LED16.anode, R16.Pin_0
  N38: LED17.anode, R17.Pin_0
  N39: LED18.anode, R18.Pin_0
  N40: LED19.anode, R19.Pin_0
  N41: LED20.anode, R20.Pin_0
  N42: LED24.anode, R24.Pin_0
  N43: LED23.anode, R23.Pin_0
  N44: LED21.anode, R21.Pin_0
  N45: LED22.anode, R22.Pin_0
  N46: J4.pin1, R24.Pin_1
  N47: J4.pin2, R23.Pin_1
  N48: J4.pin3, R22.Pin_1
  N49: J4.pin4, R21.Pin_1
