# Fritzing sketch LED (saved by Fritzing 0.9.2b)
circuit board: 1.95725cm x 1.27576cm
breadboards: 1

parts:
  D = LED - 5mm [color="Red (633nm)" package="5 mm [THT]"]
  R = Resistor [tolerance=±5% resistance=1k package=THT]
  J = female pin header, 2 pins [form="♀ (female)"]

nets:
  N1: D.cathode, J.pin2
  N2: D.anode, R.Pin_1
  N3: R.Pin_0, J.pin1

notes:
  (C) 2016 Pete R. Jemian
  Vcc
  Gnd
  1k
  BLNUHR-LED, v1.0
