# Fritzing sketch shield (saved by Fritzing 0.9.2b)
breadboards: 1

parts:
  Part1 = Arduino Mega Proto Shield
  J1 = female pin header, 24 pins [form="♀ (female)"]
  J2 = female pin header, 24 pins [form="♀ (female)"]
  R1 = Resistor [tolerance=±5% resistance=1k package=THT]
  R2 = Resistor [tolerance=±5% resistance=1k package=THT]
  R3 = Resistor [tolerance=±5% resistance=1k package=THT]
  R4 = Resistor [tolerance=±5% resistance=1k package=THT]
  R5 = Resistor [tolerance=±5% resistance=1k package=THT]
  R6 = Resistor [tolerance=±5% resistance=1k package=THT]
  R7 = Resistor [tolerance=±5% resistance=1k package=THT]
  R8 = Resistor [tolerance=±5% resistance=1k package=THT]
  R9 = Resistor [tolerance=±5% resistance=1k package=THT]
  R10 = Resistor [tolerance=±5% resistance=1k package=THT]
  R11 = Resistor [tolerance=±5% resistance=1k package=THT]
  R12 = Resistor [tolerance=±5% resistance=1k package=THT]
  R13 = Resistor [tolerance=±5% resistance=1k package=THT]
  R14 = Resistor [tolerance=±5% resistance=1k package=THT]
  R15 = Resistor [tolerance=±5% resistance=1k package=THT]
  R16 = Resistor [tolerance=±5% resistance=1k package=THT]
  R17 = Resistor [tolerance=±5% resistance=1k package=THT]
  R18 = Resistor [tolerance=±5% resistance=1k package=THT]
  R19 = Resistor [tolerance=±5% resistance=1k package=THT]
  R20 = Resistor [tolerance=±5% resistance=1k package=THT]
  R21 = Resistor [tolerance=±5% resistance=1k package=THT]
  R22 = Resistor [tolerance=±5% resistance=1k package=THT]
  R23 = Resistor [tolerance=±5% resistance=1k package=THT]
  R24 = Resistor [tolerance=±5% resistance=1k package=THT]

nets:
  N1: Part1.D53, R20.Pin_1
  N2: Part1.D51, R23.Pin_1
  N3: Part1.D22, R21.Pin_1
  N4: Part1.D24, R24.Pin_1
  N5: Part1.GND, Part1.N$52, Part1.N$69, Part1.N$76, Part1.N$93, Part1.N$100, Part1.N$117, Part1.N$124, Part1.N$146, Part1.N$153, Part1.N$174, Part1.N$181, Part1.N$202, Part1.N$209, Part1.N$230, Part1.N$237, Part1.N$258, Part1.N$265, Part1.N$286, Part1.N$293, Part1.N$324, Part1.N$336, Part1.N$345, Part1.N$369, Part1.N$378, J1.pin1, J1.pin2, J1.pin3, J1.pin4, J1.pin5, J1.pin6, J1.pin7, J1.pin8, J1.pin9, J1.pin10, J1.pin11, J1.pin12, J1.pin13, J1.pin14, J1.pin15, J1.pin16, J1.pin17, J1.pin18, J1.pin19, J1.pin20, J1.pin21, J1.pin22, J1.pin23, J1.pin24
  N6: Part1.N$53, Part1.N$54, J2.pin24, R20.Pin_0
  N7: Part1.N$67, Part1.N$68, J2.pin23, R21.Pin_0
  N8: Part1.N$77, Part1.N$78, J2.pin22, R23.Pin_0
  N9: Part1.N$91, Part1.N$92, J2.pin21, R24.Pin_0
  N10: Part1.N$101, Part1.N$102, J2.pin20, R22.Pin_0
  N11: Part1.N$106, R22.Pin_1
  N12: Part1.N$111, R19.Pin_1
  N13: Part1.N$115, Part1.N$116, J2.pin19, R19.Pin_0
  N14: Part1.N$128, Part1.N$129, J2.pin18, R15.Pin_0
  N15: Part1.N$133, R15.Pin_1
  N16: Part1.N$140, R13.Pin_1
  N17: Part1.N$144, Part1.N$145, J2.pin17, R13.Pin_0
  N18: Part1.N$154, Part1.N$155, J2.pin16, R17.Pin_0
  N19: Part1.N$159, R17.Pin_1
  N20: Part1.N$168, R18.Pin_1
  N21: Part1.N$172, Part1.N$173, J2.pin15, R18.Pin_0
  N22: Part1.N$182, Part1.N$183, J2.pin14, R14.Pin_0
  N23: Part1.N$187, R14.Pin_1
  N24: Part1.N$196, R16.Pin_1
  N25: Part1.N$200, Part1.N$201, J2.pin13, R16.Pin_0
  N26: Part1.N$210, Part1.N$211, J2.pin12, R9.Pin_0
  N27: Part1.N$215, R9.Pin_1
  N28: Part1.N$224, R7.Pin_1
  N29: Part1.N$228, Part1.N$229, J2.pin11, R7.Pin_0
  N30: Part1.N$238, Part1.N$239, J2.pin10, R8.Pin_0
  N31: Part1.N$243, R8.Pin_1
  N32: Part1.N$252, R10.Pin_1
  N33: Part1.N$256, Part1.N$257, J2.pin9, R10.Pin_0
  N34: Part1.N$266, Part1.N$267, J2.pin8, R11.Pin_0
  N35: Part1.N$271, R11.Pin_1
  N36: Part1.N$280, R12.Pin_1
  N37: Part1.N$283, Part1.N$285, J2.pin7, R12.Pin_0
  N38: Part1.N$294, Part1.N$295, J2.pin6, R6.Pin_0
  N39: Part1.N$299, R6.Pin_1
  N40: Part1.N$308, R5.Pin_1
  N41: Part1.N$312, Part1.N$325, J2.pin5, R5.Pin_0
  N42: Part1.N$330, R4.Pin_1
  N43: Part1.N$334, Part1.N$335, J2.pin4, R4.Pin_0
  N44: Part1.N$346, Part1.N$347, J2.pin3, R3.Pin_0
  N45: Part1.N$351, R3.Pin_1
  N46: Part1.N$363, R2.Pin_1
  N47: Part1.N$366, Part1.N$368, J2.pin2, R2.Pin_0
  N48: Part1.N$379, Part1.N$380, J2.pin1, R1.Pin_0
  N49: Part1.N$384, R1.Pin_1
